# Fritzing sketch two-buttons-uniLed (saved by Fritzing 0.9.3b)
breadboards: 1

parts:
  Componente2 = Arduino Uno (Rev3)
  LED13 = LED - 5mm [color="Red (633nm)" package="5 mm [THT]"]
  R12 = Resistor [tolerance=±5% resistance=330 package=THT]
  S1 = Momentary Switch [package=ksa_sealed_tac_switch]
  S2 = Momentary Switch [package=ksa_sealed_tac_switch]

nets:
  N1: Componente2.D9_PWM, LED13.anode
  N2: Componente2.GND, R12.Pin_1, S1.2, S2.2
  N3: Componente2.D2, S1.4
  N4: Componente2.D3_PWM, S2.4
  N5: LED13.cathode, R12.Pin_0
