# Fritzing sketch unicolor-led (saved by Fritzing 0.9.3b)
breadboards: 1

parts:
  LED1 = LED - 5mm [color="Red (633nm)" package="5 mm [THT]"]
  Componente1 = Arduino Uno (Rev3)
  R1 = Resistor [tolerance=±5% resistance=330 package=THT]
  R2 = Resistor [tolerance=±5% resistance=330 package=THT]
  R3 = Resistor [tolerance=±5% resistance=330 package=THT]
  R4 = Resistor [tolerance=±5% resistance=330 package=THT]
  R5 = Resistor [tolerance=±5% resistance=330 package=THT]
  R6 = Resistor [tolerance=±5% resistance=330 package=THT]
  R7 = Resistor [tolerance=±5% resistance=330 package=THT]
  R8 = Resistor [tolerance=±5% resistance=330 package=THT]
  LED2 = LED - 5mm [color="Red (633nm)" package="5 mm [THT]"]
  LED3 = LED - 5mm [color="Red (633nm)" package="5 mm [THT]"]
  LED4 = LED - 5mm [color="Red (633nm)" package="5 mm [THT]"]
  LED5 = LED - 5mm [color="Yellow (585nm)" package="5 mm [THT]"]
  LED6 = LED - 5mm [color="Yellow (585nm)" package="5 mm [THT]"]
  LED7 = LED - 5mm [color="Yellow (585nm)" package="5 mm [THT]"]
  LED8 = LED - 5mm [color="Yellow (585nm)" package="5 mm [THT]"]

nets:
  N1: LED1.cathode, R1.Pin_0
  N2: LED1.anode, Componente1.D2
  N3: Componente1.D8, LED3.anode
  N4: Componente1.D9_PWM, LED6.anode
  N5: Componente1.GND, R1.Pin_1, R2.Pin_1, R3.Pin_1, R4.Pin_1, R5.Pin_1, R6.Pin_1, R7.Pin_1, R8.Pin_1
  N6: Componente1.D3_PWM, LED8.anode
  N7: Componente1.D4, LED2.anode
  N8: Componente1.D5_PWM, LED7.anode
  N9: Componente1.D6_PWM, LED4.anode
  N10: Componente1.D7, LED5.anode
  N11: R2.Pin_0, LED8.cathode
  N12: R3.Pin_0, LED7.cathode
  N13: R4.Pin_0, LED2.cathode
  N14: R5.Pin_0, LED4.cathode
  N15: R6.Pin_0, LED5.cathode
  N16: R7.Pin_0, LED6.cathode
  N17: R8.Pin_0, LED3.cathode
